# Fritzing sketch WEATHER_STATION (saved by Fritzing 0.9.3b)

parts:
  U1 = NodeMCU V1.0
  DHT1 = DHT22 Humidity and Temperature Sensor
  YL-83_-_Detection_Board1 = YL-83 Rain Sensor - Detection Board
  YL-83_-_Control_Board1 = YL-83 Rain Sensor - Control Board
  VCC1 = 4 x AAA Battery Mount
  R2 = Resistor [tolerance=±20% resistance=10k package=THT]
  R3 = Resistor [tolerance=±5% resistance=100k package=THT]
  R1 = Photocell (LDR) [package=THT]

nets:
  N1: U1.D0, DHT1.DATA
  3V3: U1.3V3, YL-83_-_Control_Board1.VCC, R2.Pin_0, R3.Pin_1
  GND: U1.GND, DHT1.GND, YL-83_-_Control_Board1.GND, VCC1.-, R1.pin_1
  N2: U1.D5, YL-83_-_Control_Board1.DO
  N3: U1.Vin, VCC1.+
  N4: U1.A0, R3.Pin_0, R1.pin_0
  N5: DHT1.VDD, R2.Pin_1
  N6: YL-83_-_Detection_Board1.POS, YL-83_-_Control_Board1.POS
  N7: YL-83_-_Detection_Board1.NEG, YL-83_-_Control_Board1.NEG

custom parts:
  NodeMCU V1.0: ESP8266 based NodeMCU
  YL-83 Rain Sensor - Detection Board: The YL-83 is a rain sensor that has more resistance when dry and less resistance when wet. The module runs at 5V.
  YL-83 Rain Sensor - Control Board: The YL-83 is a rain sensor that has more resistance when dry and less resistance when wet. The module runs at 5V.
